// Logisim project processor.circ as structural Verilog: 21 circuits, main circuit main
module main (
  input  [3:0] in_1
);

  wire ALUSrc_Signal, and_1_out, and_2_out, ble_flag, ble_signal, bne_flag, bne_signal, Call_signal, Clock,
       clock_1_out, Clock_signal, Jump_Signal, MemRead_Signal, MemToReg_Signal, MemWrite_Signal, or_1_out,
       PCSrc_Signal, ReadSrc2_Signal, RegWrite_Signal, Return_Signal, signed_bit, Zero_Signal;
  wire [1:0] ALU_signal;
  wire [2:0] multiplexer_5_out;
  wire [3:0] control_bits;
  wire [10:0] addr_bits;
  wire [15:0] adder_1_out, adder_2_out, ALU_Output, extend_addr_bits, extend_imme_bits, multiplexer_1_out,
       multiplexer_2_out, multiplexer_4_out, multiplexer_6_out, multiplexer_7_out, multiplexer_8_out,
       new_addr, PC, r2, ra_addr, ram_2_data, received_addr, register_file_16_bit_1_data_1, subtractor_1_out;

  // Probe on multiplexer_4_out
  Multiplexer #(.width(16)) multiplexer_1 (
    .in0(extend_imme_bits), .in1(extend_addr_bits), .out(multiplexer_1_out), .sel(Jump_Signal), .en(1'b1));
  Register #(.width(16)) register_1 (.D(multiplexer_4_out), .en(1'b1), .Q(PC), .clk(Clock));  // open: clr
  // Probe on multiplexer_1_out
  RAM #(.addrWidth(16), .dataWidth(16)) ram_1 (
    .addr(PC), .data({control_bits, addr_bits, signed_bit}), .sel(1'b1), .clk(Clock));  // open: ld, clr
  Shifter #(.width(16)) shifter_1 (.in(multiplexer_1_out), .\dist (in_1), .out(received_addr));
  Adder #(.width(16)) adder_1 (.a(16'h1), .b(PC), .out(adder_1_out));  // open: cin, cout
  Adder #(.width(16)) adder_2 (.a(PC), .b(received_addr), .out(adder_2_out));  // open: cin, cout
  Subtractor #(.width(16)) subtractor_1 (.a(PC), .b(received_addr), .out(subtractor_1_out));  // open: bin, bout
  // Probe on addr_bits[2:0]
  // Probe on addr_bits[5:3]
  // Probe on signed_bit
  // Probe on control_bits
  Multiplexer #(.width(16)) multiplexer_2 (
    .in0(new_addr), .in1(ra_addr), .out(multiplexer_2_out), .sel(Return_Signal), .en(1'b1));
  Multiplexer #(.width(16)) multiplexer_3 (
    .in0(adder_2_out), .in1(subtractor_1_out), .out(new_addr), .sel(signed_bit), .en(1'b1));
  // Probe on addr_bits[8:6]
  // Probe on ra_addr
  Register #(.width(16)) register_2 (.D(adder_1_out), .en(Call_signal), .Q(ra_addr), .clk(Clock));  // open: clr
  and and_1 (and_1_out, bne_signal, bne_flag);
  and and_2 (and_2_out, ble_signal, ble_flag);
  Multiplexer #(.width(16)) multiplexer_4 (
    .in0(adder_1_out), .in1(multiplexer_2_out), .out(multiplexer_4_out), .sel(or_1_out), .en(1'b1));
  or or_1 (or_1_out, and_1_out, and_2_out, PCSrc_Signal);
  // Probe on addr_bits[10:6]
  // Probe on addr_bits
  assign extend_addr_bits = {{5{1'b0}}, addr_bits};  // Bit_Extender bit_extender_1
  Multiplexer #(.width(3)) multiplexer_5 (
    .in0(addr_bits[2:0]), .in1(addr_bits[8:6]), .out(multiplexer_5_out), .sel(ReadSrc2_Signal), .en(1'b1));
  // Probe on addr_bits[2:0]
  // Probe on addr_bits[5:3]
  // Probe on multiplexer_5_out
  // Probe on multiplexer_8_out
  Register_File_16_bit register_file_16_bit_1 (
    .Write_enable(RegWrite_Signal), .Write_Register(addr_bits[2:0]), .Register_Data(multiplexer_8_out),
    .Clock(Clock), .r1(addr_bits[5:3]), .in_7(multiplexer_5_out), .Data_1(register_file_16_bit_1_data_1),
    .Data_2(r2));  // open: Reset
  assign extend_imme_bits = {{11{1'b0}}, addr_bits[10:6]};  // Bit_Extender bit_extender_2
  // Probe on r2
  Clock clock_1 (.out(clock_1_out));
  Control control_1 (
    .in_1(control_bits), .out_2(ALU_signal), .out_3(ALUSrc_Signal), .out_4(MemRead_Signal),
    .out_5(MemWrite_Signal), .out_6(MemToReg_Signal), .out_7(RegWrite_Signal), .out_8(ble_signal),
    .out_9(bne_signal), .out_10(Jump_Signal), .out_11(PCSrc_Signal), .out_12(Clock_signal),
    .out_13(ReadSrc2_Signal), .out_14(Call_signal), .out_15(Return_Signal), .out_16(Zero_Signal));
  // Probe on ALU_Output
  and and_3 (Clock, clock_1_out, Clock_signal);
  Multiplexer #(.width(16)) multiplexer_6 (
    .in0(r2), .in1(extend_imme_bits), .out(multiplexer_6_out), .sel(ALUSrc_Signal), .en(1'b1));
  Multiplexer #(.width(16)) multiplexer_7 (
    .in0(register_file_16_bit_1_data_1), .in1({16{1'b0}}), .out(multiplexer_7_out), .sel(Zero_Signal),
    .en(1'b1));
  // Probe on multiplexer_6_out
  // Probe on ALU_signal
  RAM #(.addrWidth(16), .dataWidth(16), .bus("separate")) ram_2 (
    .addr(ALU_Output), .din(r2), .data(ram_2_data), .str(MemWrite_Signal), .sel(1'b1), .clk(Clock),
    .ld(MemRead_Signal));  // open: clr
  // Probe on multiplexer_7_out
  ALU alu_1 (
    .in_1(multiplexer_7_out), .in_2(multiplexer_6_out), .in_3(ALU_signal), .bne_flag(bne_flag),
    .ble_flag(ble_flag), .out_6(ALU_Output));
  // Probe on ram_2_data
  Multiplexer #(.width(16)) multiplexer_8 (
    .in0(ALU_Output), .in1(ram_2_data), .out(multiplexer_8_out), .sel(MemToReg_Signal), .en(1'b1));

  // Other names for the same wires on the sheet: dest_bits[2:0] = addr_bits[2:0]; scr1_bits[2:0] = addr_bits[5:3];
  //   imme_bits[4:0] = addr_bits[10:6]; scr2_bits[2:0] = addr_bits[8:6]

  // Notes on the sheet:
  //   instruc.
  //   dest
  //   src1
  //   control
  //   src2
  //   immediate
  //   address
  //   Reg
  //   data
endmodule

module ALU (
  input  [15:0] in_1,
  input  [15:0] in_2,
  input  [1:0] in_3,
  output bne_flag,
  output ble_flag,
  output [15:0] out_6
);

  wire comparator_1_eq, comparator_1_lt;
  wire [15:0] adder_1_out, and_1_out, or_1_out, subtractor_1_out;

  Adder #(.width(16)) adder_1 (.a(in_1), .b(in_2), .out(adder_1_out));  // open: cin, cout
  Subtractor #(.width(16)) subtractor_1 (.a(in_1), .b(in_2), .out(subtractor_1_out));  // open: bin, bout
  assign and_1_out = in_1 & in_2;  // AND_Gate and_1, 16 bits wide
  assign or_1_out = in_1 | in_2;  // OR_Gate or_1, 16 bits wide
  Multiplexer #(.select(2), .width(16)) multiplexer_1 (
    .in0(adder_1_out), .in1(subtractor_1_out), .in2(and_1_out), .in3(or_1_out), .out(out_6), .sel(in_3),
    .en(1'b1));
  Comparator #(.width(16)) comparator_1 (
    .a(out_6), .b({16{1'b0}}), .eq(comparator_1_eq), .lt(comparator_1_lt));  // open: gt
  not not_1 (bne_flag, comparator_1_eq);
  or or_2 (ble_flag, comparator_1_eq, comparator_1_lt);

  // Other names for the same wires on the sheet: input_1[15:0] = in_1; input_2[15:0] = in_2

  // Notes on the sheet:
  //   Input 1
  //   Input 2
  //   Control Signal
  //   ALUOp 00: Addition
  //   ALUOp 10: AND
  //   ALUOp 11: OR
  //   ALUOp 01: Substraction
  //   Output
endmodule

module Control (
  input  [3:0] in_1,
  output [1:0] out_2,
  output out_3,
  output out_4,
  output out_5,
  output out_6,
  output out_7,
  output out_8,
  output out_9,
  output out_10,
  output out_11,
  output out_12,
  output out_13,
  output out_14,
  output out_15,
  output out_16
);

  Control_ALU_0 control_alu_0_1 (.in_1(in_1), .out_2(out_2[0]));
  Control_ALU_1 control_alu_1_1 (.in_1(in_1), .out_2(out_2[1]));
  Control_ALUSrc control_alusrc_1 (.in_1(in_1), .out_2(out_3));
  Control_Memory_Read control_memory_read_1 (.in_1(in_1), .out_2(out_4));
  Control_Memory_Write control_memory_write_1 (.in_1(in_1), .out_2(out_5));
  Control_MemToReg control_memtoreg_1 (.in_1(in_1), .out_2(out_6));
  Control_Reg_Write control_reg_write_1 (.in_1(in_1), .out_2(out_7));
  Control_Branch_ble control_branch_ble_1 (.in_1(in_1), .Branch_ble(out_8));
  Control_Branch_bne control_branch_bne_1 (.in_1(in_1), .Branch_bne(out_9));
  Control_Jump control_jump_1 (.in_1(in_1), .Jump_Signal(out_10));
  Control_PC_Source control_pc_source_1 (.in_1(in_1), .PC_Source(out_11));
  Contol_Clock contol_clock_1 (.in_1(in_1), .Clock_Signal(out_12));
  Control_Readscr2 control_readscr2_1 (.in_1(in_1), .ReadSrc2(out_13));
  Control_Call control_call_1 (.in_1(in_1), .Call(out_14));
  Control_rtn control_rtn_1 (.in_1(in_1), .Return_signal(out_15));
  Control_zero control_zero_1 (.in_1(in_1), .Zero_Signal(out_16));

  // Notes on the sheet:
  //   ALU Signal
  //   ALUSrc Signal
  //   Memory Read Signal
  //   Memory Write Signal
  //   MemToReg Signal
  //   Reg Write Signal
  //   BLE Signal
  //   BNE Signal
  //   Jump Signal
  //   PCSrc Signal
  //   Clock Signal
  //   ReadSrc2 Signal
  //   Call Signal
  //   Return Signal
  //   Zero Signal
endmodule

module Control_ALU_1 (
  input  [3:0] in_1,
  output out_2
);

  wire and_1_out, and_2_out, and_3_out, and_4_out, and_5_out, not_1_out, not_2_out, not_3_out, not_4_out,
       not_5_out, not_6_out, not_7_out, not_8_out, not_9_out, not_10_out, not_11_out, not_12_out, not_13_out,
       not_14_out;

  not not_1 (not_1_out, in_1[3]);
  not not_2 (not_2_out, in_1[2]);
  and and_1 (and_1_out, not_1_out, not_2_out, not_3_out, in_1[0]);
  not not_3 (not_3_out, in_1[1]);
  not not_4 (not_4_out, in_1[3]);
  not not_5 (not_5_out, in_1[2]);
  and and_2 (and_2_out, not_4_out, not_5_out, in_1[1], not_6_out);
  not not_6 (not_6_out, in_1[0]);
  not not_7 (not_7_out, in_1[3]);
  and and_3 (and_3_out, not_7_out, in_1[2], not_8_out, not_9_out);
  not not_8 (not_8_out, in_1[1]);
  not not_9 (not_9_out, in_1[0]);
  not not_10 (not_10_out, in_1[2]);
  and and_4 (and_4_out, in_1[3], not_10_out, not_11_out, not_12_out);
  not not_11 (not_11_out, in_1[1]);
  not not_12 (not_12_out, in_1[0]);
  not not_13 (not_13_out, in_1[2]);
  and and_5 (and_5_out, in_1[3], not_13_out, not_14_out, in_1[0]);
  not not_14 (not_14_out, in_1[1]);
  or or_1 (out_2, and_1_out, and_2_out, and_3_out, and_4_out, and_5_out);

  // Other names for the same wires on the sheet: Bit_12 = in_1[0]; Bit_13 = in_1[1]; Bit_14 = in_1[2];
  //   Bit_15 = in_1[3]

  // Notes on the sheet:
  //   Opcode
  //   ALU[1] Signal
endmodule

module Control_ALU_0 (
  input  [3:0] in_1,
  output out_2
);

  wire and_1_out, and_2_out, and_3_out, and_4_out, and_5_out, not_1_out, not_2_out, not_3_out, not_4_out,
       not_5_out, not_6_out, not_7_out, not_8_out, not_9_out, not_10_out, not_11_out;

  not not_1 (not_1_out, in_1[3]);
  not not_2 (not_2_out, in_1[2]);
  and and_1 (and_1_out, not_1_out, not_2_out, in_1[1], not_3_out);
  not not_3 (not_3_out, in_1[0]);
  not not_4 (not_4_out, in_1[3]);
  and and_2 (and_2_out, not_4_out, in_1[2], not_5_out, not_6_out);
  not not_5 (not_5_out, in_1[1]);
  not not_6 (not_6_out, in_1[0]);
  not not_7 (not_7_out, in_1[2]);
  and and_3 (and_3_out, in_1[3], not_7_out, not_8_out, in_1[0]);
  not not_8 (not_8_out, in_1[1]);
  not not_9 (not_9_out, in_1[2]);
  and and_4 (and_4_out, in_1[3], not_9_out, in_1[1], not_10_out);
  not not_10 (not_10_out, in_1[0]);
  not not_11 (not_11_out, in_1[2]);
  and and_5 (and_5_out, in_1[3], not_11_out, in_1[1], in_1[0]);
  or or_1 (out_2, and_1_out, and_2_out, and_3_out, and_4_out, and_5_out);

  // Other names for the same wires on the sheet: Bit_12 = in_1[0]; Bit_13 = in_1[1]; Bit_14 = in_1[2];
  //   Bit_15 = in_1[3]

  // Notes on the sheet:
  //   Opcode
  //   ALU[0] Signal
endmodule

module Control_ALUSrc (
  input  [3:0] in_1,
  output out_2
);

  wire and_1_out, and_2_out, and_3_out, and_4_out, and_5_out, and_6_out, not_1_out, not_2_out, not_3_out,
       not_4_out, not_5_out, not_6_out, not_7_out, not_8_out, not_9_out, not_10_out, not_11_out, not_12_out,
       not_13_out;

  not not_1 (not_1_out, in_1[3]);
  and and_1 (and_1_out, not_1_out, in_1[2], not_2_out, not_3_out);
  not not_2 (not_2_out, in_1[1]);
  not not_3 (not_3_out, in_1[0]);
  not not_4 (not_4_out, in_1[3]);
  and and_2 (and_2_out, not_4_out, in_1[2], not_5_out, in_1[0]);
  not not_5 (not_5_out, in_1[1]);
  not not_6 (not_6_out, in_1[3]);
  and and_3 (and_3_out, not_6_out, in_1[2], in_1[1], not_7_out);
  not not_7 (not_7_out, in_1[0]);
  not not_8 (not_8_out, in_1[3]);
  and and_4 (and_4_out, not_8_out, in_1[2], in_1[1], in_1[0]);
  not not_9 (not_9_out, in_1[2]);
  and and_5 (and_5_out, in_1[3], not_9_out, not_10_out, not_11_out);
  not not_10 (not_10_out, in_1[1]);
  not not_11 (not_11_out, in_1[0]);
  not not_12 (not_12_out, in_1[2]);
  and and_6 (and_6_out, in_1[3], not_12_out, not_13_out, in_1[0]);
  not not_13 (not_13_out, in_1[1]);
  or or_1 (out_2, and_1_out, and_2_out, and_3_out, and_4_out, and_5_out, and_6_out);

  // Other names for the same wires on the sheet: Bit_12 = in_1[0]; Bit_13 = in_1[1]; Bit_14 = in_1[2];
  //   Bit_15 = in_1[3]

  // Notes on the sheet:
  //   Opcode
  //   ALU Source Signal
endmodule

module Control_Memory_Read (
  input  [3:0] in_1,
  output out_2
);

  wire not_1_out, not_2_out;

  not not_1 (not_1_out, in_1[3]);
  not not_2 (not_2_out, in_1[1]);
  and and_1 (out_2, not_1_out, in_1[2], not_2_out, in_1[0]);

  // Other names for the same wires on the sheet: Bit_12 = in_1[0]; Bit_13 = in_1[1]; Bit_14 = in_1[2];
  //   Bit_15 = in_1[3]

  // Notes on the sheet:
  //   Opcode
  //   Memory Read Signal
endmodule

module Control_Memory_Write (
  input  [3:0] in_1,
  output out_2
);

  wire not_1_out, not_2_out;

  not not_1 (not_1_out, in_1[3]);
  and and_1 (out_2, not_1_out, in_1[2], in_1[1], not_2_out);
  not not_2 (not_2_out, in_1[0]);

  // Other names for the same wires on the sheet: Bit_12 = in_1[0]; Bit_13 = in_1[1]; Bit_14 = in_1[2];
  //   Bit_15 = in_1[3]

  // Notes on the sheet:
  //   Opcode
  //   Memory Write Signal
endmodule

module Control_MemToReg (
  input  [3:0] in_1,
  output out_2
);

  wire not_1_out, not_2_out;

  not not_1 (not_1_out, in_1[3]);
  and and_1 (out_2, not_1_out, in_1[2], not_2_out, in_1[0]);
  not not_2 (not_2_out, in_1[1]);

  // Other names for the same wires on the sheet: Bit_12 = in_1[0]; Bit_13 = in_1[1]; Bit_14 = in_1[2];
  //   Bit_15 = in_1[3]

  // Notes on the sheet:
  //   Opcode
  //   Memory Write Signal
endmodule

module Control_Reg_Write (
  input  [3:0] in_1,
  output out_2
);

  wire and_1_out, and_2_out, and_3_out, and_4_out, and_5_out, and_6_out, and_7_out, and_8_out, and_9_out,
       not_1_out, not_2_out, not_3_out, not_4_out, not_5_out, not_6_out, not_7_out, not_8_out, not_9_out,
       not_10_out, not_11_out, not_12_out, not_13_out, not_14_out, not_15_out, not_16_out, not_17_out,
       not_18_out, not_19_out, not_20_out, not_21_out, not_22_out, not_23_out;

  not not_1 (not_1_out, in_1[3]);
  not not_2 (not_2_out, in_1[2]);
  and and_1 (and_1_out, not_1_out, not_2_out, not_3_out, not_4_out);
  not not_3 (not_3_out, in_1[1]);
  not not_4 (not_4_out, in_1[0]);
  not not_5 (not_5_out, in_1[3]);
  not not_6 (not_6_out, in_1[2]);
  and and_2 (and_2_out, not_5_out, not_6_out, not_7_out, in_1[0]);
  not not_7 (not_7_out, in_1[1]);
  not not_8 (not_8_out, in_1[3]);
  not not_9 (not_9_out, in_1[2]);
  and and_3 (and_3_out, not_8_out, not_9_out, in_1[1], not_10_out);
  not not_10 (not_10_out, in_1[0]);
  not not_11 (not_11_out, in_1[3]);
  not not_12 (not_12_out, in_1[2]);
  and and_4 (and_4_out, not_11_out, not_12_out, in_1[1], in_1[0]);
  not not_13 (not_13_out, in_1[3]);
  and and_5 (and_5_out, not_13_out, in_1[2], not_14_out, not_15_out);
  not not_14 (not_14_out, in_1[1]);
  not not_15 (not_15_out, in_1[0]);
  not not_16 (not_16_out, in_1[3]);
  and and_6 (and_6_out, not_16_out, in_1[2], not_17_out, in_1[0]);
  not not_17 (not_17_out, in_1[1]);
  not not_18 (not_18_out, in_1[3]);
  and and_7 (and_7_out, not_18_out, in_1[2], in_1[1], in_1[0]);
  not not_19 (not_19_out, in_1[2]);
  and and_8 (and_8_out, in_1[3], not_19_out, not_20_out, not_21_out);
  not not_20 (not_20_out, in_1[1]);
  not not_21 (not_21_out, in_1[0]);
  not not_22 (not_22_out, in_1[2]);
  and and_9 (and_9_out, in_1[3], not_22_out, not_23_out, in_1[0]);
  not not_23 (not_23_out, in_1[1]);
  or or_1 (out_2, and_1_out, and_2_out, and_3_out, and_4_out, and_5_out, and_6_out, and_7_out, and_8_out, and_9_out);

  // Other names for the same wires on the sheet: Bit_12 = in_1[0]; Bit_13 = in_1[1]; Bit_14 = in_1[2];
  //   Bit_15 = in_1[3]

  // Notes on the sheet:
  //   Opcode
  //   Reg Write Signal
endmodule

module Control_Branch_ble (
  input  [3:0] in_1,
  output Branch_ble
);

  wire not_1_out, not_2_out;

  not not_1 (not_1_out, in_1[2]);
  not not_2 (not_2_out, in_1[0]);
  and and_1 (Branch_ble, in_1[3], not_1_out, in_1[1], not_2_out);

  // Other names for the same wires on the sheet: Bit_12 = in_1[0]; Bit_13 = in_1[1]; Bit_14 = in_1[2];
  //   Bit_15 = in_1[3]
endmodule

module Control_Branch_bne (
  input  [3:0] in_1,
  output Branch_bne
);

  wire not_1_out;

  not not_1 (not_1_out, in_1[2]);
  and and_1 (Branch_bne, in_1[3], not_1_out, in_1[1], in_1[0]);

  // Other names for the same wires on the sheet: Bit_12 = in_1[0]; Bit_13 = in_1[1]; Bit_14 = in_1[2];
  //   Bit_15 = in_1[3]
endmodule

module Control_Jump (
  input  [3:0] in_1,
  output Jump_Signal
);

  wire and_1_out, and_2_out, and_3_out, and_4_out, and_5_out, and_6_out, and_7_out, not_1_out, not_2_out;

  not not_1 (not_1_out, in_1[0]);
  not not_2 (not_2_out, in_1[1]);
  and and_1 (and_1_out, in_1[2], in_1[3]);
  and and_2 (and_2_out, in_1[0], not_2_out);
  and and_3 (and_3_out, not_1_out, in_1[1]);
  and and_4 (and_4_out, not_2_out, not_1_out);
  and and_5 (and_5_out, and_2_out, and_1_out);
  and and_6 (and_6_out, and_3_out, and_1_out);
  and and_7 (and_7_out, and_4_out, and_1_out);
  or or_1 (Jump_Signal, and_5_out, and_6_out, and_7_out);

  // Other names for the same wires on the sheet: Bit_10 = in_1[0]; Bit_11 = in_1[1]; Bit_12 = in_1[2];
  //   Bit_13 = in_1[3]
endmodule

module Control_PC_Source (
  input  [3:0] in_1,
  output PC_Source
);

  wire and_1_out, and_2_out, and_3_out, not_1_out, not_2_out;

  not not_1 (not_1_out, in_1[0]);
  not not_2 (not_2_out, in_1[1]);
  and and_1 (and_1_out, in_1[3], in_1[2], not_2_out, not_1_out);
  and and_2 (and_2_out, in_1[3], in_1[2], not_2_out, in_1[0]);
  and and_3 (and_3_out, in_1[3], in_1[2], in_1[1], not_1_out);
  or or_1 (PC_Source, and_1_out, and_2_out, and_3_out);

  // Other names for the same wires on the sheet: Bit_12 = in_1[0]; Bit_13 = in_1[1]; Bit_14 = in_1[2];
  //   Bit_15 = in_1[3]
endmodule

module Contol_Clock (
  input  [3:0] in_1,
  output Clock_Signal
);

  wire not_1_out, not_2_out, not_3_out, not_4_out;

  not not_1 (not_1_out, in_1[3]);
  not not_2 (not_2_out, in_1[2]);
  not not_3 (not_3_out, in_1[1]);
  not not_4 (not_4_out, in_1[0]);
  or or_1 (Clock_Signal, not_1_out, not_2_out, not_3_out, not_4_out);

  // Other names for the same wires on the sheet: Bit_12 = in_1[0]; Bit_13 = in_1[1]; Bit_14 = in_1[2];
  //   Bit_15 = in_1[3]
endmodule

module Control_Readscr2 (
  input  [3:0] in_1,
  output ReadSrc2
);

  wire and_1_out, and_2_out, and_3_out, and_4_out, not_1_out, not_2_out, not_3_out, not_4_out;

  not not_1 (not_1_out, in_1[0]);
  not not_2 (not_2_out, in_1[1]);
  not not_3 (not_3_out, in_1[2]);
  not not_4 (not_4_out, in_1[3]);
  and and_1 (and_1_out, not_4_out, not_3_out, not_2_out, not_1_out);
  and and_2 (and_2_out, not_4_out, not_3_out, not_2_out, in_1[0]);
  and and_3 (and_3_out, not_4_out, not_3_out, in_1[1], not_1_out);
  and and_4 (and_4_out, not_4_out, not_3_out, in_1[1], in_1[0]);
  or or_1 (ReadSrc2, and_1_out, and_2_out, and_3_out, and_4_out);
  Control_Call control_call_1 ();  // open: in_1, Call

  // Other names for the same wires on the sheet: Bit_12 = in_1[0]; Bit_13 = in_1[1]; Bit_14 = in_1[2];
  //   Bit_15 = in_1[3]
endmodule

module Control_Call (
  input  [3:0] in_1,
  output Call
);

  wire not_1_out;

  not not_1 (not_1_out, in_1[1]);
  and and_1 (Call, in_1[0], not_1_out, in_1[2], in_1[3]);

  // Other names for the same wires on the sheet: Bit_12 = in_1[0]; Bit_13 = in_1[1]; Bit_14 = in_1[2];
  //   Bit_15 = in_1[3]
endmodule

module Control_rtn (
  input  [3:0] in_1,
  output Return_signal
);

  wire not_1_out;

  not not_1 (not_1_out, in_1[0]);
  and and_1 (Return_signal, not_1_out, in_1[1], in_1[2], in_1[3]);

  // Other names for the same wires on the sheet: Bit_12 = in_1[0]; Bit_13 = in_1[1]; Bit_14 = in_1[2];
  //   Bit_15 = in_1[3]
endmodule

module Control_zero (
  input  [3:0] in_1,
  output Zero_Signal
);

  wire and_1_out, and_2_out, not_1_out, not_2_out, not_3_out, not_4_out, not_5_out;

  not not_1 (not_1_out, in_1[3]);
  not not_2 (not_2_out, in_1[2]);
  not not_3 (not_3_out, in_1[3]);
  not not_4 (not_4_out, in_1[1]);
  not not_5 (not_5_out, in_1[0]);
  and and_1 (and_1_out, not_1_out, not_2_out, in_1[1], in_1[0]);
  and and_2 (and_2_out, not_3_out, in_1[2], not_4_out, not_5_out);
  or or_1 (Zero_Signal, and_1_out, and_2_out);

  // Other names for the same wires on the sheet: Bit_12 = in_1[0]; Bit_13 = in_1[1]; Bit_14 = in_1[2];
  //   Bit_15 = in_1[3]

  // Notes on the sheet:
  //   Opcode
endmodule

module Register_File_16_bit (
  input  Write_enable,
  input  [2:0] Write_Register,
  input  [15:0] Register_Data,
  input  Clock,
  input  Reset,
  input  [2:0] r1,
  input  [2:0] in_7,
  output [15:0] Data_1,
  output [15:0] Data_2
);

  wire and_1_out, and_2_out, and_3_out, and_4_out, and_5_out, and_6_out, and_7_out, and_8_out,
       decoder_1_out0, decoder_1_out1, decoder_1_out2, decoder_1_out3, decoder_1_out4, decoder_1_out5,
       decoder_1_out6, decoder_1_out7;
  wire [15:0] register_1_q, register_2_q, register_3_q, register_4_q, register_5_q, register_6_q,
       register_7_q, register_8_q;

  Decoder #(.select(3)) decoder_1 (
    .out0(decoder_1_out0), .out1(decoder_1_out1), .out2(decoder_1_out2), .out3(decoder_1_out3),
    .out4(decoder_1_out4), .out5(decoder_1_out5), .out6(decoder_1_out6), .out7(decoder_1_out7),
    .sel(Write_Register), .en(1'b1));
  and and_1 (and_1_out, Write_enable, decoder_1_out0);
  and and_2 (and_2_out, Write_enable, decoder_1_out1);
  and and_3 (and_3_out, Write_enable, decoder_1_out2);
  and and_4 (and_4_out, Write_enable, decoder_1_out3);
  and and_5 (and_5_out, Write_enable, decoder_1_out4);
  and and_6 (and_6_out, Write_enable, decoder_1_out5);
  and and_7 (and_7_out, Write_enable, decoder_1_out6);
  and and_8 (and_8_out, Write_enable, decoder_1_out7);
  Register #(.width(16)) register_1 (.D(Register_Data), .en(and_1_out), .Q(register_1_q), .clk(Clock), .clr(Reset));
  Register #(.width(16)) register_2 (.D(Register_Data), .en(and_2_out), .Q(register_2_q), .clk(Clock), .clr(Reset));
  Register #(.width(16)) register_3 (.D(Register_Data), .en(and_3_out), .Q(register_3_q), .clk(Clock), .clr(Reset));
  Register #(.width(16)) register_4 (.D(Register_Data), .en(and_4_out), .Q(register_4_q), .clk(Clock), .clr(Reset));
  Register #(.width(16)) register_5 (.D(Register_Data), .en(and_5_out), .Q(register_5_q), .clk(Clock), .clr(Reset));
  Register #(.width(16)) register_6 (.D(Register_Data), .en(and_6_out), .Q(register_6_q), .clk(Clock), .clr(Reset));
  Register #(.width(16)) register_7 (.D(Register_Data), .en(and_7_out), .Q(register_7_q), .clk(Clock), .clr(Reset));
  Register #(.width(16)) register_8 (.D(Register_Data), .en(and_8_out), .Q(register_8_q), .clk(Clock), .clr(Reset));
  Multiplexer #(.select(3), .width(16)) multiplexer_1 (
    .in0(register_1_q), .in1(register_2_q), .in2(register_3_q), .in3(register_4_q), .in4(register_5_q),
    .in5(register_6_q), .in6(register_7_q), .in7(register_8_q), .out(Data_1), .sel(r1), .en(1'b1));
  Multiplexer #(.select(3), .width(16)) multiplexer_2 (
    .in0(register_1_q), .in1(register_2_q), .in2(register_3_q), .in3(register_4_q), .in4(register_5_q),
    .in5(register_6_q), .in6(register_7_q), .in7(register_8_q), .out(Data_2), .sel(in_7), .en(1'b1));

  // Notes on the sheet:
  //   Read Register 1
  //   Read Register 2
endmodule

module Split_Test (
  input  [15:0] in_1,
  input  in_2,
  input  in_3,
  input  in_4,
  input  in_5,
  input  in_6,
  input  in_7,
  input  [15:0] in_8,
  input  in_9,
  input  [15:0] _9,
  input  [15:0] _9_2,
  input  [15:0] _9_3
);

  wire and_1_out, and_2_out, or_1_out, or_2_out;
  wire [15:0] controlled_buffer_1_out, extend_addr_bits;

  or or_1 (or_1_out, in_3, in_5);
  // Probe on controlled_buffer_1_out
  assign controlled_buffer_1_out = or_1_out ? in_1 : 16'bz;  // Controlled_Buffer controlled_buffer_1
  assign controlled_buffer_1_out = in_9 ? in_8 : 16'bz;  // Controlled_Buffer controlled_buffer_2
  // Probe on _9_3[3:1]
  // Probe on _9_3[6:4]
  // Probe on _9_3[15:12]
  // Probe on _9_3[9:7]
  // Probe on {_9[0], _9[15:14]}
  // Probe on _9_2[3:1]
  // Probe on _9_2[6:4]
  // Probe on _9_2[15:12]
  // Probe on _9[3:1]
  // Probe on _9[6:4]
  // Probe on _9[9:7]
  // Probe on _9[9:7]
  // Probe on _9[13:10]
  and and_1 (and_1_out, in_2, in_4);
  or or_2 (or_2_out, and_1_out, and_2_out);
  and and_2 (and_2_out, in_6, in_7);
  // Probe on _9_2[9:7]
  // Probe on _9_3[11:7]
  // Probe on _9_3[11:1]
  assign extend_addr_bits = {{5{1'b0}}, _9_3[11:1]};  // Bit_Extender bit_extender_1
  // Probe on {_9_2[0], _9_2[11:7]}
  // Probe on {_9_2[0], _9_2[11:1]}

  // Other names for the same wires on the sheet: signed_bit = _9_3[0]; control_bits[3:0] = _9_3[15:12];
  //   addr_bits[10:0] = _9_3[11:1]; dest_bits[2:0] = _9_3[3:1]; scr1_bits[2:0] = _9_3[6:4];
  //   imme_bits[4:0] = _9_3[11:7]; scr2_bits[2:0] = _9_3[9:7]

  // Notes on the sheet:
  //   6
  //   3
  //   pass extend imme/ addr
  //   6
  //   3
  //   6
  //   3
  //   dest
  //   src1
  //   control
  //   control
  //   src2
  //   dest
  //   src1
  //   scr2
  //   control
  //   dest
  //   src1
  //   bne, ble
  //   immediate
  //   src2
  //   immediate
  //   address
  //   immediate
endmodule
